# Fritzing sketch wiring (saved by Fritzing 0.9.3b)

parts:
  Mod1 = Raspberry Pi Pico W
  DHT1 = Humidity and Temperature Sensor DHT11
  R1 = Resistor [tolerance=±5% resistance=220 package=THT]
  Grove1 = Grove OLED 128x96

nets:
  N1: Mod1.pin_4, Grove1.SDA
  N2: Mod1.pin_5, Grove1.SCL
  N3: Mod1.pin_20, DHT1.Data-signal, R1.Pin_1
  VCC: Mod1.pin_36, DHT1.Vcc, R1.Pin_0, Grove1.VCC
  N4: Mod1.pin_38, DHT1.GND_2, Grove1.GND

custom parts:
  Raspberry Pi Pico W: Raspberry Pi Pico W. Based around the RP2040 microcontroller the Pico W is a low cost microcontroller device bringing Raspberry Pi quality, cost, and easy of use to the microcontroller space. The areas marked KEEPOUT in pcb silkscreen should not have traces running through them to avoid shorts on a soldered in module!
  Humidity and Temperature Sensor DHT11: Digital relative humidity & temperature sensor DHT11
